# Fritzing sketch airQ (saved by Fritzing 0.9.3b)

parts:
  MCU1 = Raspberry Pi Zero
  ZS-042_RTC1 = ZS-042 RTC Module

nets:
  N1: MCU1.pin_1, MCU1.pin_2, MCU1.pin_3, MCU1.pin_4, ZS-042_RTC1.VCC, ZS-042_RTC1.SDA
  N2: MCU1.pin_5, MCU1.pin_6, MCU1.pin_9, MCU1.pin_10, ZS-042_RTC1.GND, ZS-042_RTC1.SCL
